# Fritzing sketch circuit (saved by Fritzing 0.9.6b)
breadboards: 1

parts:
  Raspberry_Pi_1 = Raspberry Pi 4 [part_number=RPI-4-b]
  KY-1 = Keyes Relay [package=THT]
  R1 = Resistor [tolerance=±5% resistance=220 package="0805 [SMD]"]
  S2 = Round Pushbutton
  S3 = Round Pushbutton
  S4 = Round Pushbutton
  S5 = Round Pushbutton
  S6 = Round Pushbutton
  M2 = DC Motor
  LED1 = LED - 5mm [color="Red (633nm)" current=0.030 package="5 mm [THT]"]

nets:
  3V3: Raspberry_Pi_1.3v3, Raspberry_Pi_1.3V3, KY-1.power, KY-1.C
  N1: Raspberry_Pi_1.GPIO3, S2.leg1
  N2: Raspberry_Pi_1.GPIO17, S5.leg1
  N3: Raspberry_Pi_1.GPIO27, S6.leg1
  N4: Raspberry_Pi_1.GPIO22, Raspberry_Pi_1.GPIO23, R1.Pin_1
  N5: Raspberry_Pi_1.GPIO6, Raspberry_Pi_1.GPIO12, KY-1.signal
  N6: Raspberry_Pi_1.GPIO13, S3.leg1
  N7: Raspberry_Pi_1.GPIO19, S4.leg1
  N8: Raspberry_Pi_1.GND, KY-1.ground, M2.pin_1
  N9: KY-1.NO, M2.pin_2
  N10: S4.leg0, LED1.cathode

custom parts:
  Raspberry Pi 4: The RPi4, a faster version of the awesome Raspberry Pi 2 B ARM Board with 40 pin gpio. Ready for special Raspberry Pi B+ and RPi2 Hat (Hardware attached (on) top)
  Keyes Relay: The Keyes 5V relay module is suitable for SCM development, home appliance control. It uses a 5V~12V TIL control signal which can control DC / AC signal.
